# Fritzing sketch ESP8266 (saved by Fritzing 0.9.3b)
breadboards: 1

parts:
  J2 = Generic shrouded header - 8 pins [form="♂ (shrouded male)" package=THT]
  Q1 = Basic FET N-Channel [package="DPak [SMD]"]
  Part1 = Arduino Uno (Rev3) - ICSP
  D1 = LTE-302 [package=lte-302]

nets:
  N1: J2.pin1, J2.pin3, Q1.drain
  N2: J2.pin4, Part1.D1/TX
  N3: J2.pin5, Part1.D0/RX
  N4: J2.pin6, J2.pin8, Q1.Gate, Part1.GND, D1.C
  N5: J2.pin7, D1.A
  N6: Q1.source, Part1.5V

custom parts:
  Generic shrouded header - 8 pins: Generic shrouded header
